# Fritzing sketch PiCarRouting (saved by Fritzing 0.9.3b)
circuit board: 3.78896cm x 5.47664cm

parts:
  Raspberry_Pi_3 = Raspberry Pi 3 [part_number=RPI-3-V1.2]
  STEERING = Basic Servo
  SER_CAM = Basic Servo
  M1 = DC Motor
  M2 = DC Motor
  INDI_LEFT = RGB LED (com. cathode, rbg) [package="5 mm [THT]"]
  EXPW = Battery block 12V
  SP1 = SPEAKER [package=pcb_mount_speaker]
  INDI_RIGH = RGB LED (com. cathode, rbg) [package="5 mm [THT]"]
  U1 = L298_BRIDGE_DRIVER [package=powerso20]

nets:
  GND: Raspberry_Pi_3.GND, STEERING.gnd, SER_CAM.gnd, INDI_LEFT.common_cathode, EXPW.-, SP1.-, INDI_RIGH.common_cathode, U1.GND
  N1: Raspberry_Pi_3.GIPO17, INDI_RIGH.green_anode
  N2: Raspberry_Pi_3.GIPO27, INDI_RIGH.blue_anode
  N3: Raspberry_Pi_3.GIPO22, INDI_RIGH.red_anode
  N4: Raspberry_Pi_3.GIPO5, INDI_LEFT.green_anode
  N5: Raspberry_Pi_3.GIPO6, INDI_LEFT.blue_anode
  N6: Raspberry_Pi_3.GIPO13, INDI_LEFT.red_anode
  N7: Raspberry_Pi_3.GIPO26, SP1.+
  N8: Raspberry_Pi_3.GIPO21, U1.IN4
  N9: Raspberry_Pi_3.GIPO20, U1.IN3
  N10: Raspberry_Pi_3.GIPO16, U1.IN2
  N11: Raspberry_Pi_3.GIPO12, U1.IN1
  N12: Raspberry_Pi_3.GIPO15, SER_CAM.pulse
  N13: Raspberry_Pi_3.GIPO14, STEERING.pulse
  VCC: Raspberry_Pi_3.5V, STEERING.vcc, SER_CAM.vcc, U1.ENA, U1.ENB
  N14: M1.pin_1, U1.OUT1
  N15: M1.pin_2, U1.OUT2
  N16: M2.pin_1, U1.OUT3
  N17: M2.pin_2, U1.OUT4
  N18: EXPW.+, U1.VS

custom parts:
  Battery block 12V: Your standard 12 Volts battery block
