# Fritzing sketch RemoteControllerRouting (saved by Fritzing 0.9.3b)
stripboards: 2

parts:
  WeMos_D1 = WeMos D1 Mini
  Part1 = Arduino Uno (Rev3)
  BUZZER = Piezo Speaker
  LEFT_BTN = Pushbutton [package="[THT]"]
  R1 = Resistor [tolerance=±5% resistance=1k package=THT]
  BUZZ_BTN = Pushbutton [package="[THT]"]
  R2 = Resistor [tolerance=±5% resistance=1k package=THT]
  BUZZ_BTN1 = Pushbutton [package="[THT]"]
  R3 = Resistor [tolerance=±5% resistance=1k package=THT]
  BUZZ_BTN2 = Pushbutton [package="[THT]"]
  R4 = Resistor [tolerance=±5% resistance=1k package=THT]
  WHEEL = Rotary Encoder [package=THT]
  GL3 = Rotary Encoder [package=THT]
  HANDBRAKE = Rotary Encoder [package=THT]
  GR3 = Rotary Encoder [package=THT]
  BRAKE = Rotary Encoder [package=THT]
  SPEED = Rotary Encoder [package=THT]
  LEFT = smd LED [color="Blue (430nm)" package="1206 [SMD]"]
  BUZZ = smd LED [color="Blue (430nm)" package="1206 [SMD]"]
  PARK = smd LED [color="Blue (430nm)" package="1206 [SMD]"]
  RIGH = smd LED [color="Blue (430nm)" package="1206 [SMD]"]

nets:
  5V: WeMos_D1.5V, Part1.VIN
  N1: WeMos_D1.D4, Part1.D3_PWM
  N2: WeMos_D1.D5, Part1.D2
  N3: WeMos_D1.G, Part1.GND, BUZZER.pin1, R1.Pin_1, R2.Pin_1, R3.Pin_1, R4.Pin_1, WHEEL.EncoderPinB, GL3.EncoderPinB, HANDBRAKE.EncoderPinB, GR3.EncoderPinB, BRAKE.EncoderPinB, SPEED.EncoderPinB, LEFT.cathode, BUZZ.cathode, PARK.cathode, RIGH.cathode
  N4: Part1.A0, SPEED.EncoderPinC
  N5: Part1.A1, BRAKE.EncoderPinC
  N6: Part1.A2, GR3.EncoderPinC
  N7: Part1.A3, HANDBRAKE.EncoderPinC
  N8: Part1.A4/SDA, GL3.EncoderPinC
  N9: Part1.A5/SCL, WHEEL.EncoderPinC
  N10: Part1.D9_PWM, BUZZER.pin2
  N11: Part1.D10_PWM/SS, RIGH.anode
  N12: Part1.D11_PWM/MOSI, PARK.anode
  N13: Part1.D12/MISO, BUZZ.anode
  N14: Part1.D13/SCK, LEFT.anode
  N15: Part1.D4, BUZZ_BTN2.Pin_1, BUZZ_BTN2.Pin_2, R4.Pin_0
  N16: Part1.D5_PWM, BUZZ_BTN1.Pin_1, BUZZ_BTN1.Pin_2, R3.Pin_0
  N17: Part1.D6_PWM, BUZZ_BTN.Pin_1, BUZZ_BTN.Pin_2, R2.Pin_0
  N18: Part1.D7, LEFT_BTN.Pin_1, LEFT_BTN.Pin_2, R1.Pin_0
  N19: Part1.5V, LEFT_BTN.Pin_3, LEFT_BTN.Pin_4, BUZZ_BTN.Pin_3, BUZZ_BTN.Pin_4, BUZZ_BTN1.Pin_3, BUZZ_BTN1.Pin_4, BUZZ_BTN2.Pin_3, BUZZ_BTN2.Pin_4, WHEEL.EncoderPinA, GL3.EncoderPinA, HANDBRAKE.EncoderPinA, GR3.EncoderPinA, BRAKE.EncoderPinA, SPEED.EncoderPinA
