# Fritzing sketch arduino&wemos (saved by Fritzing 0.9.3b)
stripboards: 2

parts:
  ARDUINO_UNO_R3 = Arduino Uno (Rev3) - ICSP
  ESP8266_WEMOS_D1 = WeMos D1 Mini
  Left_turn_signal_indicator = LED - 5mm [color="Red (633nm)" package="5 mm [THT]"]
  Buzzer_indicator = LED - 5mm [color="Red (633nm)" package="5 mm [THT]"]
  Parking_mode_indicator = LED - 5mm [color="Red (633nm)" package="5 mm [THT]"]
  Right_turn_signal_indicator = LED - 5mm [color="Red (633nm)" package="5 mm [THT]"]
  Right_turn_signal_indicator_button = Pushbutton [package="[THT]"]
  Parking_mode_button = Pushbutton [package="[THT]"]
  Buzzer_button = Pushbutton [package="[THT]"]
  Left_turn_signal_indicator_button = Pushbutton [package="[THT]"]
  R1 = Resistor [tolerance=±5% resistance=1k package=THT]
  R2 = Resistor [tolerance=±5% resistance=1k package=THT]
  R3 = Resistor [tolerance=±5% resistance=1k package=THT]
  R4 = Resistor [tolerance=±5% resistance=1k package=THT]
  Buzzer = Piezo Speaker
  Accelerator = Rotary Encoder [package=THT]
  Brake_pedal = Rotary Encoder [package=THT]
  Gear_stick_backward = Rotary Encoder [package=THT]
  Handbreak = Rotary Encoder [package=THT]
  Gear_stick_forward = Rotary Encoder [package=THT]
  Steering_wheel = Rotary Encoder [package=THT]

nets:
  N1: ARDUINO_UNO_R3.A0, Accelerator.EncoderPinC
  N2: ARDUINO_UNO_R3.A1, Brake_pedal.EncoderPinC
  N3: ARDUINO_UNO_R3.A2, Gear_stick_backward.EncoderPinC
  N4: ARDUINO_UNO_R3.A3, Handbreak.EncoderPinC
  N5: ARDUINO_UNO_R3.A4/SDA, Gear_stick_forward.EncoderPinC
  N6: ARDUINO_UNO_R3.A5/SCL, Steering_wheel.EncoderPinC
  N7: ARDUINO_UNO_R3.5V, Left_turn_signal_indicator.cathode, Buzzer_indicator.cathode, Parking_mode_indicator.cathode, Right_turn_signal_indicator.cathode, R1.Pin_1, R2.Pin_1, R3.Pin_1, R4.Pin_1, Accelerator.EncoderPinB, Brake_pedal.EncoderPinB, Gear_stick_backward.EncoderPinB, Handbreak.EncoderPinB, Gear_stick_forward.EncoderPinB, Steering_wheel.EncoderPinB
  N8: ARDUINO_UNO_R3.D9_PWM, Buzzer.pin2
  N9: ARDUINO_UNO_R3.D10_PWM/SS, Right_turn_signal_indicator.anode
  N10: ARDUINO_UNO_R3.D11_PWM/MOSI, Parking_mode_indicator.anode
  N11: ARDUINO_UNO_R3.D12/MISO, Buzzer_indicator.anode
  N12: ARDUINO_UNO_R3.D13/SCK, Left_turn_signal_indicator.anode
  N13: ARDUINO_UNO_R3.GND, ARDUINO_UNO_R3.D4, ESP8266_WEMOS_D1.G, Right_turn_signal_indicator_button.Pin_1, Right_turn_signal_indicator_button.Pin_2, Right_turn_signal_indicator_button.Pin_3, Right_turn_signal_indicator_button.Pin_4, Parking_mode_button.Pin_1, Parking_mode_button.Pin_2, Buzzer_button.Pin_1, Buzzer_button.Pin_2, Left_turn_signal_indicator_button.Pin_1, Left_turn_signal_indicator_button.Pin_2, R4.Pin_0, Buzzer.pin1, Accelerator.EncoderPinA, Brake_pedal.EncoderPinA, Gear_stick_backward.EncoderPinA, Handbreak.EncoderPinA, Gear_stick_forward.EncoderPinA, Steering_wheel.EncoderPinA
  N14: ARDUINO_UNO_R3.D2, ESP8266_WEMOS_D1.D5
  N15: ARDUINO_UNO_R3.D3_PWM, ESP8266_WEMOS_D1.D4
  N16: ARDUINO_UNO_R3.D5_PWM, Parking_mode_button.Pin_3, Parking_mode_button.Pin_4, R3.Pin_0
  N17: ARDUINO_UNO_R3.D6_PWM, Buzzer_button.Pin_3, Buzzer_button.Pin_4, R2.Pin_0
  N18: ARDUINO_UNO_R3.D7, Left_turn_signal_indicator_button.Pin_3, Left_turn_signal_indicator_button.Pin_4, R1.Pin_0
  VIN: ARDUINO_UNO_R3.VIN, ESP8266_WEMOS_D1.5V

// code stored in the sketch: Untitled.ino

