# Fritzing sketch demo controller (saved by Fritzing 0.9.3b)
breadboards: 1

parts:
  Part1 = Arduino Uno (Rev3) - ICSP
  WeMos_D1_Mini1 = WeMos D1 Mini
  S3 = Pushbutton [package="[THT]"]
  R7 = Resistor [tolerance=±5% resistance=220 package=THT]
  LED3 = LED - 5mm [color="Red (633nm)" package="5 mm [THT]"]
  R8 = Resistor [tolerance=±5% resistance=220 package=THT]
  LED4 = LED - 5mm [color="Red (633nm)" package="5 mm [THT]"]
  S4 = Pushbutton [package="[THT]"]
  R9 = Resistor [tolerance=±5% resistance=220 package=THT]
  R10 = Resistor [tolerance=±5% resistance=220 package=THT]

nets:
  N1: Part1.5V, S3.Pin_3, S3.Pin_4, S4.Pin_1, S4.Pin_2, R9.Pin_0
  N2: Part1.D12/MISO, LED4.cathode
  N3: Part1.D13/SCK, LED3.cathode
  N4: Part1.D2, WeMos_D1_Mini1.D5
  N5: Part1.D3_PWM, WeMos_D1_Mini1.D4
  N6: Part1.D4, R9.Pin_1
  N7: Part1.D5_PWM, R7.Pin_1
  N8: Part1.GND, S3.Pin_1, S3.Pin_2, R7.Pin_0, R8.Pin_1, S4.Pin_3, S4.Pin_4, R10.Pin_1
  N9: LED3.anode, R8.Pin_0
  N10: LED4.anode, R10.Pin_0
