# Fritzing sketch esp8266 (saved by Fritzing 0.9.3b)
breadboards: 1

parts:
  Part1 = Arduino Uno (Rev3) - ICSP
  U1 = ESP8266 WiFi Module [part_number=ESP8266]

nets:
  N1: Part1.D2, U1.RXD
  N2: Part1.D3_PWM, U1.TXD
  5V: Part1.5V, U1.VCC, U1.CH_PD
  GND: Part1.GND, U1.GND
